// Digital circuit circuito_exp2_ativ2_digital.dig as structural Verilog
module circuito_exp2_ativ2_digital (
  input  CLOCK,
  input  ZERA,
  input  CARREGA,
  input  CONTA,
  input  [3:0] DADO,
  output MENOR,
  output MAIOR,
  output IGUAL,
  output FIM,
  output [3:0] CONTAGEM
);

  circuito_exp2_ativ2 #(.applicationType("IVERILOG")) u_circuito_exp2_ativ2 (
    .clock(CLOCK), .zera(ZERA), .carrega(CARREGA), .conta(CONTA), .chaves(DADO), .menor(MENOR),
    .maior(MAIOR), .igual(IGUAL), .fim(FIM), .db_contagem(CONTAGEM));
endmodule

/* Code of circuito_exp2_ativ2:
module circuito_exp2_ativ2 (clock, zera, carrega, conta, chaves, 
                            menor, maior, igual, fim, db_contagem);
    input        clock;
    input        zera;
    input        carrega;
    input        conta;
    input  [3:0] chaves;
    output       menor;
    output       maior;
    output       igual;
    output       fim;
    output [3:0] db_contagem;

    wire   [3:0] s_contagem;  // sinal interno para interligacao dos componentes

    // contador_163
    contador_163 contador (
      .clock( clock ),
      .clr  ( ~zera ), // feito por mim
      .ld   ( ~carrega ),
      .ent  ( 1'b1 ),
      .enp  ( conta ),
      .D    ( chaves ), // feito por mim
      .Q    ( s_contagem ),
      .rco  ( fim ) // feito por mim
    );

    // comparador_85
    comparador_85 comparador (
      .A   ( s_contagem ), // feito por mim
      .B   ( chaves ), // feito por mim
      .ALBi( 1'b0 ), // feito por mim
      .AGBi( 1'b0 ),
      .AEBi( 1'b1 ),
      .ALBo( menor ), // feito por mim
      .AGBo( maior ), // feito por mim
      .AEBo( igual ) // feito por mim
    );

    // saida de depuracao
    assign db_contagem = s_contagem;

 endmodule

module comparador_85 (ALBi, AGBi, AEBi, A, B, ALBo, AGBo, AEBo);

    input[3:0] A, B;
    input      ALBi, AGBi, AEBi;
    output     ALBo, AGBo, AEBo;
    wire[4:0]  CSL, CSG;

    assign CSL  = ~A + B + ALBi;
    assign ALBo = ~CSL[4];
    assign CSG  = A + ~B + AGBi;
    assign AGBo = ~CSG[4];
    assign AEBo = ((A == B) && AEBi);

endmodule /* comparador_85 * /

module contador_163 ( clock, clr, ld, ent, enp, D, Q, rco );
    input clock, clr, ld, ent, enp;
    input [3:0] D;
    output reg [3:0] Q = 1'b0;
    output reg rco;

    always @ (posedge clock)
        if (~clr)               Q <= 4'd0;
        else if (~ld)           Q <= D;
        else if (ent && enp)    Q <= Q + 1'b1;
        else                    Q <= Q;
 
    always @ (Q or ent)
        if (ent && (Q == 4'd15))   rco = 1;
        else                       rco = 0;
endmodule
*/
