// Digital circuit circuito_exp2_ativ2_letraj_digital.dig as structural Verilog
module circuito_exp2_ativ2_letraj_digital (
  input  CLOCK,
  input  ZERA,
  input  CARREGA,
  input  CONTA,
  input  [3:0] DADO,
  output [3:0] CONTAGEM,
  output FIM,
  output MENOR,
  output MAIOR,
  output IGUAL
);

  wire not_1_out, not_2_out;

  not not_1 (not_1_out, ZERA);
  not not_2 (not_2_out, CARREGA);
  contador_163 #(.applicationType("IVERILOG")) u_contador_163 (
    .clock(CLOCK), .clr(not_1_out), .ld(not_2_out), .ent(CONTA), .enp(1'b1), .D(DADO), .Q(CONTAGEM), .rco(FIM));
  comparador_85 #(.applicationType("IVERILOG")) u_comparador_85 (
    .A(CONTAGEM), .B(DADO), .ALBi(1'b0), .AGBi(1'b0), .AEBi(1'b1), .ALBo(MENOR), .AGBo(MAIOR), .AEBo(IGUAL));
endmodule

/* Code of contador_163:
module contador_163 ( clock, clr, ld, ent, enp, D, Q, rco );
    input clock, clr, ld, ent, enp;
    input [3:0] D;
    output reg [3:0] Q = 1'b0;
    output reg rco;

    always @ (posedge clock)
        if (~clr)               Q <= 4'd0;
        else if (~ld)           Q <= D;
        else if (ent && enp)    Q <= Q + 1'b1;
        else                    Q <= Q;
 
    always @ (Q or ent)
        if (ent && (Q == 4'd15))   rco = 1;
        else                       rco = 0;
endmodule
*/

/* Code of comparador_85:
module comparador_85 (ALBi, AGBi, AEBi, A, B, ALBo, AGBo, AEBo);

    input[3:0] A, B;
    input      ALBi, AGBi, AEBi;
    output     ALBo, AGBo, AEBo;
    wire[4:0]  CSL, CSG;

    assign CSL  = ~A + B + ALBi;
    assign ALBo = ~CSL[4];
    assign CSG  = A + ~B + AGBi;
    assign AGBo = ~CSG[4];
    assign AEBo = ((A == B) && AEBi);

endmodule /* comparador_85 * /
*/
