// Digital circuit circuito_exp2_desafio.dig as structural Verilog
module circuito_exp2_desafio (
  input  CLOCK,
  input  ZERA,
  input  CARREGA,
  input  CONTA,
  input  [3:0] DADO,
  output MENOR,
  output MAIOR,
  output IGUAL,
  output FIM,
  output [6:0] CONTAGEM
);

  wire [7:0] not_1_out;

  circuito_exp2_desafio #(.applicationType("IVERILOG")) u_circuito_exp2_desafio (
    .clock(CLOCK), .zera(ZERA), .carrega(CARREGA), .conta(CONTA), .chaves(DADO), .menor(MENOR),
    .maior(MAIOR), .igual(IGUAL), .fim(FIM), .db_contagem(CONTAGEM));
  assign not_1_out = ~{1'b0, CONTAGEM};  // Not not_1, 8 bits wide
  Seven_Seg seven_seg_1 (
    .a(not_1_out[0]), .b(not_1_out[1]), .c(not_1_out[2]), .d(not_1_out[3]), .e(not_1_out[4]),
    .f(not_1_out[5]), .g(not_1_out[6]), .dp(not_1_out[7]));
endmodule

/* Code of circuito_exp2_desafio:
module circuito_exp2_desafio (clock, zera, carrega, conta, chaves, 
                            menor, maior, igual, fim, db_contagem);
    input        clock;
    input        zera;
    input        carrega;
    input        conta;
    input  [3:0] chaves;
    output       menor;
    output       maior;
    output       igual;
    output       fim;
    output [6:0] db_contagem;

    wire   [3:0] s_contagem;  // sinal interno para interligacao dos componentes

    // contador_163
    contador_163 contador (
      .clock( clock ),
      .clr  ( ~zera ), // feito por mim
      .ld   ( ~carrega ),
      .ent  ( 1'b1 ),
      .enp  ( conta ),
      .D    ( chaves ), // feito por mim
      .Q    ( s_contagem ),
      .rco  ( fim ) // feito por mim
    );

    // comparador_85
    comparador_85 comparador (
      .A   ( s_contagem ), // feito por mim
      .B   ( chaves ), // feito por mim
      .ALBi( 1'b0 ), // feito por mim
      .AGBi( 1'b0 ),
      .AEBi( 1'b1 ),
      .ALBo( menor ), // feito por mim
      .AGBo( maior ), // feito por mim
      .AEBo( igual ) // feito por mim
    );

    // hexa7seg

    hexa7seg hexa7segmentos (
      .hexa( s_contagem ), // feito por mim
      .display( db_contagem ) // feito por mim
    );

 endmodule

module comparador_85 (ALBi, AGBi, AEBi, A, B, ALBo, AGBo, AEBo);

    input[3:0] A, B;
    input      ALBi, AGBi, AEBi;
    output     ALBo, AGBo, AEBo;
    wire[4:0]  CSL, CSG;

    assign CSL  = ~A + B + ALBi;
    assign ALBo = ~CSL[4];
    assign CSG  = A + ~B + AGBi;
    assign AGBo = ~CSG[4];
    assign AEBo = ((A == B) && AEBi);

endmodule /* comparador_85 * /

module contador_163 ( clock, clr, ld, ent, enp, D, Q, rco );
    input clock, clr, ld, ent, enp;
    input [3:0] D;
    output reg [3:0] Q = 1'b0;
    output reg rco;

    always @ (posedge clock)
        if (~clr)               Q <= 4'd0;
        else if (~ld)           Q <= D;
        else if (ent && enp)    Q <= Q + 1'b1;
        else                    Q <= Q;
 
    always @ (Q or ent)
        if (ent && (Q == 4'd15))   rco = 1;
        else                       rco = 0;
endmodule

module hexa7seg (hexa, display);
    input      [3:0] hexa;
    output reg [6:0] display;

    /*
     *    ---
     *   | 0 |
     * 5 |   | 1
     *   |   |
     *    ---
     *   | 6 |
     * 4 |   | 2
     *   |   |
     *    ---
     *     3
     * /
        
    always @(hexa)
    case (hexa)
        4'h0:    display = 7'b1000000;
        4'h1:    display = 7'b1111001;
        4'h2:    display = 7'b0100100;
        4'h3:    display = 7'b0110000;
        4'h4:    display = 7'b0011001;
        4'h5:    display = 7'b0010010;
        4'h6:    display = 7'b0000010;
        4'h7:    display = 7'b1111000;
        4'h8:    display = 7'b0000000;
        4'h9:    display = 7'b0010000;
        4'ha:    display = 7'b0001000;
        4'hb:    display = 7'b0000011;
        4'hc:    display = 7'b1000110;
        4'hd:    display = 7'b0100001;
        4'he:    display = 7'b0000110;
        4'hf:    display = 7'b0001110;
        default: display = 7'b1111111;
    endcase
endmodule
*/
