// Digital circuit exp6_T3BB1_atividade1_digital.dig as structural Verilog
module exp6_T3BB1_atividade1_digital (
  input  CLOCK,
  input  Memoria_a_ser_Jogada,
  input  Nivel_de_Dificuldade,
  output [6:0] CONTAGEM,
  output [6:0] SEQUENCIA,
  output [6:0] ESTADO,
  output [6:0] MEMORIA,
  output [6:0] JOGADA_FEITA,
  output PRONTO,
  output C__eq__M,
  output E__eq__S,
  output db__clock,
  output db__tem__jogada,
  output db__fimS,
  output db__seletor__memoria,
  output db__timeout,
  output db__timeoutL
);

  wire JOGAR_out, RESET_out, u_jogo_desafio_memoria_ganhou, u_jogo_desafio_memoria_perdeu,
       u_jogo_desafio_memoria_timeout;
  wire [3:0] BOTOES_0_p1, u_jogo_desafio_memoria_leds;
  wire [7:0] not_1_out, not_2_out, not_3_out, not_4_out, not_5_out;

  Button RESET (.out(RESET_out));
  Button JOGAR (.out(JOGAR_out));
  // ButtonLED BOTOES_0: pin names not known; wires that end beside it: BOTOES_0_p1[0], 1'b1
  // ButtonLED BOTOES_1: pin names not known; wires that end beside it: BOTOES_0_p1[1], 1'b1
  // ButtonLED BOTOES_2: pin names not known; wires that end beside it: BOTOES_0_p1[2], 1'b1
  jogo_desafio_memoria #(.applicationType("IVERILOG"), .iverilogOptions("-I \"/home/baunilha/Repositories/PCS3635/experiment_06/deasafio_exp6/\"")) u_jogo_desafio_memoria (
    .clock(CLOCK), .reset(RESET_out), .jogar(JOGAR_out), .botoes(BOTOES_0_p1),
    .memoria(Memoria_a_ser_Jogada), .nivel(Nivel_de_Dificuldade), .ganhou(u_jogo_desafio_memoria_ganhou),
    .perdeu(u_jogo_desafio_memoria_perdeu), .timeout(u_jogo_desafio_memoria_timeout), .pronto(PRONTO),
    .leds(u_jogo_desafio_memoria_leds), .db_clock(db__clock), .db_tem_jogada(db__tem__jogada),
    .db_chavesIgualMemoria(C__eq__M), .db_enderecoIgualSequencia(E__eq__S), .db_fimS(db__fimS),
    .db_contagem(CONTAGEM), .db_memoria(MEMORIA), .db_jogadafeita(JOGADA_FEITA), .db_sequencia(SEQUENCIA),
    .db_estado(ESTADO), .db_seletor_memoria(db__seletor__memoria), .db_timeout(db__timeout),
    .db_timeoutL(db__timeoutL));
  // ButtonLED BOTOES_3: pin names not known; wires that end beside it: BOTOES_0_p1[3], 1'b1
  LED LEDS_0 (.in(u_jogo_desafio_memoria_leds[0]));
  LED LEDS_1 (.in(u_jogo_desafio_memoria_leds[1]));
  LED LEDS_2 (.in(u_jogo_desafio_memoria_leds[2]));
  LED LEDS_3 (.in(u_jogo_desafio_memoria_leds[3]));
  assign not_1_out = ~{1'b0, CONTAGEM};  // Not not_1, 8 bits wide
  assign not_2_out = ~{1'b0, JOGADA_FEITA};  // Not not_2, 8 bits wide
  LED GANHOU (.in(u_jogo_desafio_memoria_ganhou));
  LED PERDEU (.in(u_jogo_desafio_memoria_perdeu));
  LED TIMEOUT (.in(u_jogo_desafio_memoria_timeout));
  Seven_Seg seven_seg_1 (
    .a(not_1_out[0]), .b(not_1_out[1]), .c(not_1_out[2]), .d(not_1_out[3]), .e(not_1_out[4]),
    .f(not_1_out[5]), .g(not_1_out[6]), .dp(not_1_out[7]));
  Seven_Seg seven_seg_2 (
    .a(not_2_out[0]), .b(not_2_out[1]), .c(not_2_out[2]), .d(not_2_out[3]), .e(not_2_out[4]),
    .f(not_2_out[5]), .g(not_2_out[6]), .dp(not_2_out[7]));
  assign not_3_out = ~{1'b0, MEMORIA};  // Not not_3, 8 bits wide
  assign not_4_out = ~{1'b0, SEQUENCIA};  // Not not_4, 8 bits wide
  assign not_5_out = ~{1'b0, ESTADO};  // Not not_5, 8 bits wide
  Seven_Seg seven_seg_3 (
    .a(not_3_out[0]), .b(not_3_out[1]), .c(not_3_out[2]), .d(not_3_out[3]), .e(not_3_out[4]),
    .f(not_3_out[5]), .g(not_3_out[6]), .dp(not_3_out[7]));
  Seven_Seg seven_seg_4 (
    .a(not_4_out[0]), .b(not_4_out[1]), .c(not_4_out[2]), .d(not_4_out[3]), .e(not_4_out[4]),
    .f(not_4_out[5]), .g(not_4_out[6]), .dp(not_4_out[7]));
  Seven_Seg seven_seg_5 (
    .a(not_5_out[0]), .b(not_5_out[1]), .c(not_5_out[2]), .d(not_5_out[3]), .e(not_5_out[4]),
    .f(not_5_out[5]), .g(not_5_out[6]), .dp(not_5_out[7]));

  // Notes on the sheet:
  //   CLOCK: Hz: 1000
  //   Nivel_de_Dificuldade: default 1
endmodule

/* Code of jogo_desafio_memoria:
// --- Start of jogo_desafio_memoria.v ---
//------------------------------------------------------------------
// Arquivo   : jogo_desafio_memoria.v
// Projeto   : Experiencia 6 - Jogo da Memória
//------------------------------------------------------------------
// Descricao : Circuito da Experiência 6
//             
//------------------------------------------------------------------
// Revisoes  :
//     Data        Versao  Autor             Descricao
//     25/01/2025  1.0     Ana Vitória       versao inicial
//------------------------------------------------------------------
//


module jogo_desafio_memoria (
    input clock,
    input reset,
    input jogar,
    input [3:0] botoes,
    input memoria,
    input nivel,
    output ganhou,
    output perdeu,
    output timeout,
    output pronto,
    output [3:0] leds,
    output db_clock,
    output db_tem_jogada,
    output db_chavesIgualMemoria,
    output db_enderecoIgualSequencia,
    output db_fimS,
    output [6:0] db_contagem,
    output [6:0] db_memoria,
    output [6:0] db_jogadafeita,
    output [6:0] db_sequencia,
    output [6:0] db_estado,
    output db_seletor_memoria,
    // Nossos debugs
    output db_timeout,
    output db_timeoutL
);

    wire [3:0] s_jogadafeita;
    wire [3:0] s_contagem;
    wire [3:0] s_memoria;
    wire [3:0] s_estado;
    wire [3:0] s_sequencia;
    wire s_tem_jogada;
    wire s_fimE;
    wire s_fimS;
    wire s_igualE;
    wire s_fim_timeout;
    wire s_contaT;
    wire s_contaS;
    wire s_zeraS;
    wire s_contaE;
    wire s_zeraE;
    wire s_igualS;
    wire s_zeraR;
    wire s_registraR;
    wire s_nivel;
    wire s_zeraT;
    wire s_timeoutL;
    wire s_menorS;
    wire s_controla_leds;
    wire s_zeraT_leds;
    wire s_contaT_leds;
    wire s_fase_preview;
    wire s_memoria_uc;

    // Fluxo de Dados
    exp6_fluxo_dados FD (
        .clock                     ( clock              ),
        .botoes                    ( botoes             ),
        .nivel                     ( s_nivel            ),
        .zeraT                     ( s_zeraT            ),
        .zeraR                     ( s_zeraR            ),
        .registraR                 ( s_registraR        ),
        .contaE                    ( s_contaE           ),
        .contaS                    ( s_contaS           ),
        .contaT                    ( s_contaT           ),
        .zeraE                     ( s_zeraE            ),
        .zeraS                     ( s_zeraS            ),
        .controla_leds             ( s_controla_leds    ),
        .zeraT_leds                ( s_zeraT_leds       ),
        .contaT_leds               ( s_contaT_leds      ),
        .fase_preview              ( s_fase_preview     ),
        .seletor_memoria           ( s_memoria_uc       ),
        .igual                     ( s_igualE           ),
        .enderecoIgualSequencia    ( s_igualS           ),
        .fimE                      ( s_fimE             ),
        .fimS                      ( s_fimS             ),
        .db_contagem               ( s_contagem         ),
        .db_jogadafeita            ( s_jogadafeita      ),
        .db_memoria                ( s_memoria          ),
        .tem_jogada                ( s_tem_jogada       ),
        .controle_timeout          ( s_fim_timeout      ),
        .db_sequencia              ( s_sequencia        ),
        .controle_timeout_led      ( s_timeoutL         ),
        .sequenciaMenorQueEndereco ( s_menorS           ),
        .leds                      ( leds               ),
        .db_seletor_memoria        ( db_seletor_memoria )
    );

    // Unidade de Controle
    exp6_unidade_controle UC (
        .clock         ( clock          ),
        .reset         ( reset          ),
        .jogar         ( jogar          ),
        .nivel         ( nivel          ),
        .fimE          ( s_fimE         ),
        .igualE        ( s_igualE       ),
        .igualS        ( s_igualS       ),
        .tem_jogada    ( s_tem_jogada   ),
        .timeout       ( s_fim_timeout  ),
        .timeoutL      ( s_timeoutL     ),
        .menorS        ( s_menorS       ),
        .memoria       ( memoria        ),
        .zeraE         ( s_zeraE        ),
        .contaE        ( s_contaE       ),
        .zeraS         ( s_zeraS        ),
        .contaS        ( s_contaS       ),
        .zeraR         ( s_zeraR        ),
        .registraR     ( s_registraR    ),
        .ganhou        ( ganhou         ),
        .perdeu        ( perdeu         ),
        .pronto        ( pronto         ),
        .db_estado     ( s_estado       ),
        .deu_timeout   ( timeout        ),
        .contaT        ( s_contaT       ),
        .nivel_uc      ( s_nivel        ),
        .zeraT         ( s_zeraT        ),
        .controla_leds ( s_controla_leds),
        .zeraT_leds    ( s_zeraT_leds   ),
        .contaT_leds   ( s_contaT_leds  ),
        .fase_preview  ( s_fase_preview ),
        .memoria_uc    ( s_memoria_uc   )
    );

    // Display das botoes
    hexa7seg HEX2 (
        .hexa    ( s_jogadafeita  ),
        .display ( db_jogadafeita )
    );

    // Display dos endereços codificados
    hexa7seg HEX0 (
        .hexa    ( s_contagem  ),
        .display ( db_contagem )
    );

    // Display do conteúdo em uma posição de memória
    hexa7seg HEX1 (
        .hexa    ( s_memoria  ),
        .display ( db_memoria )
    );

    // Display do estado atual
    hexa7seg HEX5 (
        .hexa    ( s_estado  ),
        .display ( db_estado )
    );

    // Display da sequência atual
    hexa7seg HEX3 (
        .hexa    ( s_sequencia  ),
        .display ( db_sequencia )
    );

assign db_chavesIgualMemoria = s_igualE;
assign db_enderecoIgualSequencia = s_igualS;
assign db_fimS = s_fimS;
assign db_tem_jogada = s_tem_jogada;
assign db_clock = clock;
assign db_timeout = s_fim_timeout;
assign db_timeoutL = s_timeoutL;
endmodule

// --- End of jogo_desafio_memoria.v ---

// --- Start of comparador_85.v ---
/* -----------------------------------------------------------------
 *  Arquivo   : comparador_85.v
 *  Projeto   : Experiencia 2 - Um Fluxo de Dados Simples
 * -----------------------------------------------------------------
 * Descricao : comparador de magnitude de 4 bits 
 *             similar ao CI 7485
 *             baseado em descricao comportamental disponivel em	
 * https://web.eecs.umich.edu/~jhayes/iscas.restore/74L85b.v
 * -----------------------------------------------------------------
 * Revisoes  :
 *     Data        Versao  Autor             Descricao
 *     21/12/2023  1.0     Edson Midorikawa  criacao
 * -----------------------------------------------------------------
 * /

module comparador_85 (ALBi, AGBi, AEBi, A, B, ALBo, AGBo, AEBo);

    input[3:0] A, B;
    input      ALBi, AGBi, AEBi;
    output     ALBo, AGBo, AEBo;
    wire[4:0]  CSL, CSG;

    assign CSL  = ~A + B + ALBi;
    assign ALBo = ~CSL[4];
    assign CSG  = A + ~B + AGBi;
    assign AGBo = ~CSG[4];
    assign AEBo = ((A == B) && AEBi);

endmodule /* comparador_85 * /
// --- End of comparador_85.v ---

// --- Start of contador_163.v ---
//------------------------------------------------------------------
// Arquivo   : contador_163.v
// Projeto   : Experiencia 2 - Um Fluxo de Dados Simples
//------------------------------------------------------------------
// Descricao : Contador binario de 4 bits, modulo 16
//             similar ao componente 74163
//
// baseado no componente Vrcntr4u.v do livro Digital Design Principles 
// and Practices, Fifth Edition, by John F. Wakerly              
//------------------------------------------------------------------
// Revisoes  :
//     Data        Versao  Autor             Descricao
//     14/12/2023  1.0     Edson Midorikawa  versao inicial
//------------------------------------------------------------------
//
module contador_163 ( clock, clr, ld, ent, enp, D, Q, rco );
    input clock, clr, ld, ent, enp;
    input [3:0] D;
    output reg [3:0] Q;
    output reg rco;

    always @ (posedge clock)
        if (~clr)               Q <= 4'd0;
        else if (~ld)           Q <= D;
        else if (ent && enp)    Q <= Q + 1'b1;
        else                    Q <= Q;
 
    always @ (Q or ent)
        if (ent && (Q == 4'd15))   rco = 1;
        else                       rco = 0;
endmodule
// --- End of contador_163.v ---

// --- Start of contador_m.v ---

/*---------------Laboratorio Digital-------------------------------------
 * Arquivo   : contador_m.v
 * Projeto   : Experiencia 4 - Desenvolvimento de Projeto de 
 *                             Circuitos Digitais em FPGA
 *-----------------------------------------------------------------------
 * Descricao : contador binario, modulo m, com parametros 
 *             M (modulo do contador) e N (numero de bits),
 *             sinais para clear assincrono (zera_as) e sincrono (zera_s)
 *             e saidas de fim e meio de contagem
 *             
 *-----------------------------------------------------------------------
 * Revisoes  :
 *     Data        Versao  Autor             Descricao
 *     30/01/2024  1.0     Edson Midorikawa  criacao
 *     16/01/2025  1.1     Edson Midorikawa  revisao
 *-----------------------------------------------------------------------
 * /

module contador_m #(parameter M=100, N=7)
  (
   input  wire          clock,
   input  wire          zera_as,
   input  wire          zera_s,
   input  wire          conta,
   output reg  [N-1:0]  Q,
   output reg           fim,
   output reg           meio
  );

  always @(posedge clock or posedge zera_as) begin
    if (zera_as) begin
      Q <= 0;
    end else if (clock) begin
      if (zera_s) begin
        Q <= 0;
      end else if (conta) begin
        if (Q == M-1) begin
          Q <= 0;
        end else begin
          Q <= Q + 1'b1;
        end
      end
    end
  end

  // Saidas
  always @ (Q)
      if (Q == M-1)   fim = 1;
      else            fim = 0;

  always @ (Q)
      if (Q == M/2-1) meio = 1;
      else             meio = 0;

endmodule

// --- End of contador_m.v ---

// --- Start of edge_detector.v ---
/* ------------------------------------------------------------------------
 *  Arquivo   : edge_detector.v
 *  Projeto   : Experiencia 4 - Desenvolvimento de Projeto de
 *                              Circuitos Digitais com FPGA
 * ------------------------------------------------------------------------
 *  Descricao : detector de borda
 *              gera um pulso na saida de 1 periodo de clock
 *              a partir da detecao da borda de subida sa entrada
 *
 *              sinal de reset ativo em alto
 *
 *              > codigo adaptado a partir de codigo VHDL disponivel em
 *                https://surf-vhdl.com/how-to-design-a-good-edge-detector/
 * ------------------------------------------------------------------------
 *  Revisoes  :
 *      Data        Versao  Autor             Descricao
 *      26/01/2024  1.0     Edson Midorikawa  versao inicial
 * ------------------------------------------------------------------------
 * /

module edge_detector (
    input  clock,
    input  reset,
    input  sinal,
    output pulso
);

    reg reg0;
    reg reg1;

    always @(posedge clock or posedge reset) begin
        if (reset) begin
            reg0 <= 1'b0;
            reg1 <= 1'b0;
        end else if (clock) begin
            reg0 <= sinal;
            reg1 <= reg0;
        end
    end

    assign pulso = ~reg1 & reg0;

endmodule

// --- End of edge_detector.v ---

// --- Start of exp6_fluxo_dados.v ---
//------------------------------------------------------------------
// Arquivo   : exp4_fluxo_dados.v
// Projeto   : Experiencia 6 - Jogo da Memória
//------------------------------------------------------------------
// Descricao : Fluxo de Dados da Experiência 6
//             
//------------------------------------------------------------------
// Revisoes  :
//     Data        Versao  Autor             Descricao
//     25/01/2025  1.0     Ana Vitória       versao inicial
//------------------------------------------------------------------
//

module exp6_fluxo_dados (
    input clock,
    input [3:0] botoes,
    input nivel,
    input zeraT,
    input zeraR,
    input registraR,
    input contaE,
    input contaS,
    input contaT,
    input zeraE,
    input zeraS,
    input controla_leds,
    input zeraT_leds,
    input contaT_leds,
    input fase_preview,
    input seletor_memoria,
    output igual,
    output enderecoIgualSequencia,
    output fimE,
    output fimS,
    output tem_jogada,
    output [3:0] db_contagem,
    output [3:0] db_jogadafeita,
    output [3:0] db_memoria,
    output controle_timeout,
    output [3:0] db_sequencia,
    output controle_timeout_led,
    output sequenciaMenorQueEndereco,
    output [3:0] leds,
    output db_seletor_memoria
);

    wire [3:0] s_endereco;
    wire [3:0] s_dado;
    wire [3:0] s_botoes;
    wire [3:0] s_sequencia;
    wire [3:0] s_sequencia_fixo;
    wire s_tem_jogada = |botoes;
    wire rco;
    wire [3:0] s_mux;
    wire [3:0] s_mem1;
    wire [3:0] s_mem2;

    // mux
    mux2x1 mux (
        .D0 (&s_endereco[2:0]),
        .D1 (rco),
        .SEL (nivel),
        .OUT (fimE)
    );

    // mux n
    mux2x1_n #( .BITS(4) ) mux_leds (
      .D0(botoes),
      .D1(s_mux),
      .SEL(fase_preview),
      .OUT(leds)
    );

    // mux n
    mux2x1_n #( .BITS(4) ) mux_zera (
      .D0(4'b0000),
      .D1(s_dado),
      .SEL(controla_leds),
      .OUT(s_mux)
    );

    // contador endereços
    contador_163 contEnd (
        .clock (clock),
        .clr   (~zeraE),
        .ld    (1'b1),
        .ent   (1'b1),
        .enp   (contaE),
        .D     (4'b0),
        .Q     (s_endereco),
        .rco   (rco)
    );

    // contador sequencias
    contador_163 contLmt (
        .clock (clock),
        .clr   (~zeraS),
        .ld    (1'b1),
        .ent   (1'b1),
        .enp   (contaS),
        .D     (4'b0),
        .Q     (s_sequencia),
        .rco   (fimS)
    );

    // comparador jogadas
    comparador_85 compJog (
        .A    (s_dado),
        .B    (s_botoes),
        .ALBi (1'b0),
        .AGBi (1'b0),
        .AEBi (1'b1),
        .ALBo (),
        .AGBo (),
        .AEBo (igual)
    );

    // comparador sequencias
    comparador_85 compLmt (
        .A    (s_sequencia),
        .B    (s_endereco),
        .ALBi (1'b0),
        .AGBi (1'b0),
        .AEBi (1'b1),
        .ALBo (sequenciaMenorQueEndereco),
        .AGBo (),
        .AEBo (enderecoIgualSequencia)
    );

    mux2x1_n #( .BITS(4) ) mux_jogo (
      .D0(s_mem1),
      .D1(s_mem2),
      .SEL(seletor_memoria),
      .OUT(s_dado)
    );

    // memória 1
    sync_rom_16x4 #(.ROM_FILE("jogo_1.mem")) memoria1 (
        .clock    (clock),
        .address  (s_endereco),
        .data_out (s_mem1)
    );

    // memória 2
    sync_rom_16x4 #(.ROM_FILE("jogo_2.mem")) memoria2 (
        .clock    (clock),
        .address  (s_endereco),
        .data_out (s_mem2)
    );

    // registrador
    registrador_4 regBotoes (
        .clock  (clock),
        .clear  (zeraR),
        .enable (registraR),
        .D      (botoes),
        .Q      (s_botoes)
    );

    edge_detector detector (
        .clock (clock),
        .reset (zeraS),
        .sinal (s_tem_jogada),
        .pulso (tem_jogada)
    );

    contador_m #(.M(5000), .N(13)) contador_timeout_jogadas (
        .clock   (clock),
        .zera_as (zeraC || zeraR),
        .zera_s  (zeraT),
        .conta   (contaT),
        .Q       (),
        .fim     (controle_timeout),
        .meio    ()
    );

    contador_m #(.M(500), .N(9)) contador_timeout_leds (
        .clock   (clock),
        .zera_as (zeraC || zeraR),
        .zera_s  (zeraT_leds),
        .conta   (contaT_leds),
        .Q       (),
        .fim     (controle_timeout_led),
        .meio    ()
    );

    assign db_memoria  = s_dado;
    assign db_contagem = s_endereco;
    assign db_sequencia = s_sequencia;
    assign db_jogadafeita = s_botoes;
    assign db_seletor_memoria = seletor_memoria;
endmodule

// --- End of exp6_fluxo_dados.v ---

// --- Start of exp6_unidade_controle.v ---
//------------------------------------------------------------------
// Arquivo   : exp6_unidade_controle.v
// Projeto   : Experiencia 6 - Jogo da Memória
//------------------------------------------------------------------
// Descricao : Unidade de controle
//         
//------------------------------------------------------------------
// Revisoes  :
//     Data        Versao  Autor                        Descricao
//     14/01/2024  1.0     Edson Midorikawa             versao inicial
//     12/01/2025  1.1     Edson Midorikawa             revisao
//     24/01/2025  1.2     Ana Murad, Heitor Gama       exercício
//------------------------------------------------------------------
//
module exp6_unidade_controle (
    input clock,
    input reset,
    input jogar,
    input nivel,
    input fimE,
    input igualE,
    input igualS,
    input tem_jogada,
    input timeout,
    input timeoutL,
    input menorS,
    input memoria,
    output reg zeraE,
    output reg contaE,
    output reg zeraS,
    output reg contaS,
    output reg zeraR,
    output reg registraR,
    output reg ganhou,
    output reg perdeu,
    output reg pronto,
    output reg [3:0] db_estado,
    output reg deu_timeout,
    output reg contaT,
    output reg nivel_uc,
    output reg zeraT,
    output reg controla_leds,
    output reg zeraT_leds,
    output reg contaT_leds,
    output reg fase_preview,
    output reg memoria_uc
);

    // Define estados
    parameter inicial        = 4'b0000;  // 0
    parameter preparacao     = 4'b0001;  // 1
    parameter nova_seq       = 4'b0010;  // 2
    parameter mostra_leds    = 4'b1011;  // B
    parameter mostrou_led    = 4'b1100;  // C
    parameter espera_led     = 4'b0111;  // 7
    parameter zera_timeout   = 4'b1000;  // 8
    parameter comecar_rodada = 4'b1101;  // D
    parameter espera         = 4'b0011;  // 3
    parameter registra       = 4'b0100;  // 4
    parameter comparacao     = 4'b0101;  // 5
    parameter proximo        = 4'b0110;  // 6
    parameter fim_erro       = 4'b1110;  // E
    parameter fim_acerto     = 4'b1010;  // A
    parameter fim_timeout    = 4'b1111;  // F

    // Variaveis de estado
    reg [3:0] Eatual, Eprox;

    reg [14*8-1:0] Eatual_str;
    always@(Eatual) begin
        case(Eatual)
            inicial:        Eatual_str = "inicial";
            preparacao:     Eatual_str = "preparacao";
            nova_seq:       Eatual_str = "nova_seq";
            mostra_leds:    Eatual_str = "mostra_leds";
            mostrou_led:    Eatual_str = "mostrou_leds";
            espera_led:     Eatual_str = "espera_leds";
            zera_timeout:   Eatual_str = "zera_timeout";
            comecar_rodada: Eatual_str = "comecar_rodada";
            espera:         Eatual_str = "espera";
            registra:       Eatual_str = "registra";
            comparacao:     Eatual_str = "comparacao";
            proximo:        Eatual_str = "proximo";
            fim_acerto:     Eatual_str = "fim_acerto";
            fim_erro:       Eatual_str = "fim_erro";
            fim_timeout:    Eatual_str = "fim_timeout";
            default:        Eatual_str = "UNKNOWN";
        endcase
    end

    // Memoria de estado
    always @(posedge clock or posedge reset) begin
        if (reset)
            Eatual <= inicial;
        else
            Eatual <= Eprox;
    end

    // Logica de proximo estado
    always @* begin
        case (Eatual)
            inicial:        Eprox = jogar ? preparacao : inicial;
            preparacao:     Eprox = mostra_leds;
            nova_seq:       Eprox = espera_led;
            mostra_leds:    Eprox = timeoutL ? (fimE ? comecar_rodada : mostrou_led) : mostra_leds;
            mostrou_led:    Eprox = espera_led;
            espera_led:     Eprox = menorS ? comecar_rodada : (timeoutL ? zera_timeout : espera_led);
            zera_timeout:   Eprox = mostra_leds;
            comecar_rodada: Eprox = espera;
            espera:         Eprox = timeout ? fim_timeout : (tem_jogada ? registra : espera);
            registra:       Eprox = comparacao;
            comparacao:     Eprox = igualE ? (fimE ? fim_acerto : (igualS ? nova_seq : proximo)) : fim_erro;
            proximo:        Eprox = espera;
            fim_acerto:     Eprox = jogar ? preparacao : fim_acerto;
            fim_erro:       Eprox = jogar ? preparacao : fim_erro;
            fim_timeout:    Eprox = jogar ? preparacao : fim_timeout;
            default:        Eprox = inicial;
        endcase
    end

    // Logica de saida (maquina Moore)
    always @* begin
        zeraE         = (Eatual == inicial || Eatual == preparacao || Eatual == nova_seq || Eatual == comecar_rodada) ? 1'b1 : 1'b0;
        zeraR         = (Eatual == inicial) ? 1'b1 : 1'b0;
        registraR     = (Eatual == registra) ? 1'b1 : 1'b0;
        contaE        = (Eatual == proximo || Eatual == mostrou_led) ? 1'b1 : 1'b0;
        pronto        = (Eatual == fim_acerto || Eatual == fim_erro || Eatual == fim_timeout) ? 1'b1 : 1'b0;
        ganhou        = (Eatual == fim_acerto) ? 1'b1 : 1'b0;
        perdeu        = (Eatual == fim_erro || Eatual == fim_timeout) ? 1'b1 : 1'b0;
        deu_timeout   = (Eatual == fim_timeout) ? 1'b1 : 1'b0;
        contaT        = (Eatual == espera) ? 1'b1: 1'b0;
        zeraS         = (Eatual == preparacao) ? 1'b1 : 1'b0;
        contaS        = (Eatual == nova_seq) ? 1'b1 : 1'b0;
        nivel_uc      = (Eatual == preparacao) ? nivel : nivel_uc;
		zeraT         = (Eatual == proximo || Eatual == nova_seq) ? 1'b1 : 1'b0;
        controla_leds = (Eatual == mostra_leds) ? 1'b1 : 1'b0;
        zeraT_leds    = (Eatual == mostrou_led || Eatual == comecar_rodada || Eatual == zera_timeout) ? 1'b1 : 1'b0;
        contaT_leds   = (Eatual == mostra_leds || Eatual == espera_led) ? 1'b1 : 1'b0;
        fase_preview  = (Eatual == mostra_leds || Eatual == mostrou_led || Eatual == zera_timeout || Eatual == comecar_rodada) ? 1'b1 : 1'b0;
        memoria_uc    = (Eatual == preparacao) ? memoria : memoria_uc;

        // Saida de depuracao (estado)
        case (Eatual)
            inicial:        db_estado = 4'b0000;  // 0
            preparacao:     db_estado = 4'b0001;  // 1
            nova_seq:       db_estado = 4'b0010;  // 2
            mostra_leds:    db_estado = 4'b1011;  // B
            mostrou_led:    db_estado = 4'b1100;  // C
            espera_led:     db_estado = 4'b0111;  // 7
            zera_timeout:   db_estado = 4'b1000;  // 8
            comecar_rodada: db_estado = 4'b1101;  // D
            espera:         db_estado = 4'b0011;  // 3
            registra:       db_estado = 4'b0100;  // 4
            comparacao:     db_estado = 4'b0101;  // 5
            proximo:        db_estado = 4'b0110;  // 6
            fim_acerto:     db_estado = 4'b1010;  // A
            fim_erro:       db_estado = 4'b1110;  // E
            fim_timeout:    db_estado = 4'b1111;  // F (deu ruim)
            default:        db_estado = 4'b1001;  // 9
        endcase
    end
endmodule
// --- End of exp6_unidade_controle.v ---

// --- Start of hexa7seg.v ---
/* ----------------------------------------------------------------
 * Arquivo   : hexa7seg.v
 * Projeto   : Experiencia 2 - Um Fluxo de Dados Simples
 *--------------------------------------------------------------
 * Descricao : decodificador hexadecimal para 
 *             display de 7 segmentos 
 * 
 * entrada : hexa - codigo binario de 4 bits hexadecimal
 * saida   : sseg - codigo de 7 bits para display de 7 segmentos
 *
 * baseado no componente bcd7seg.v da Intel FPGA
 *--------------------------------------------------------------
 * dica de uso: mapeamento para displays da placa DE0-CV
 *              bit 6 mais significativo é o bit a esquerda
 *              p.ex. sseg(6) -> HEX0[6] ou HEX06
 *--------------------------------------------------------------
 * Revisoes  :
 *     Data        Versao  Autor             Descricao
 *     24/12/2023  1.0     Edson Midorikawa  criacao
 *--------------------------------------------------------------
 * /

module hexa7seg (hexa, display);
    input      [3:0] hexa;
    output reg [6:0] display;

    /*
     *    ---
     *   | 0 |
     * 5 |   | 1
     *   |   |
     *    ---
     *   | 6 |
     * 4 |   | 2
     *   |   |
     *    ---
     *     3
     * /
        
    always @(hexa)
    case (hexa)
        4'h0:    display = 7'b1000000;
        4'h1:    display = 7'b1111001;
        4'h2:    display = 7'b0100100;
        4'h3:    display = 7'b0110000;
        4'h4:    display = 7'b0011001;
        4'h5:    display = 7'b0010010;
        4'h6:    display = 7'b0000010;
        4'h7:    display = 7'b1111000;
        4'h8:    display = 7'b0000000;
        4'h9:    display = 7'b0010000;
        4'ha:    display = 7'b0001000;
        4'hb:    display = 7'b0000011;
        4'hc:    display = 7'b1000110;
        4'hd:    display = 7'b0100001;
        4'he:    display = 7'b0000110;
        4'hf:    display = 7'b0001110;
        default: display = 7'b1111111;
    endcase
endmodule

// --- End of hexa7seg.v ---

// --- Start of jogo_desafio_memoria_tb1.v ---
`timescale 1us/1ns

module jogo_desafio_memoria_tb1;

    // Sinais para conectar com o DUT
    reg        clock_in   = 1;
    reg        reset_in   = 0;
    reg        jogar_in = 0;
    reg  [3:0] botoes_in  = 4'b0000;
    reg        nivel_in = 1;
    reg        memoria_in = 0;

    wire       ganhou_out;
    wire       perdeu_out;
    wire       pronto_out;
    wire [3:0] leds_out;
    wire       db_clock_out;
    wire       db_tem_jogada_out;
    wire       db_chavesIgualMemoria_out;
    wire       db_enderecoIgualSequencia_out;
    wire       db_fimS_out;
    wire [6:0] db_contagem_out;
    wire [6:0] db_memoria_out;
    wire [6:0] db_jogadafeita_out;
    wire [6:0] db_sequencia_out;
    wire [6:0] db_estado_out;
    wire       db_timeout_out;
    wire       db_timeoutL_out;
    wire       db_seletor_memoria_out;

    // Configuração do clock
    parameter clockPeriod = 1000; // in us, f=1KHz

    // Identificação do caso de teste
    reg [31:0] caso = 0;

    // Gerador de clock
    always #((clockPeriod / 2)) clock_in = ~clock_in;

    // Instanciação do DUT
    jogo_desafio_memoria dut (
        .clock(clock_in),
        .reset(reset_in),
        .jogar(jogar_in),
        .botoes(botoes_in),
        .nivel(nivel_in),
        .memoria(memoria_in),
        .ganhou(ganhou_out),
        .perdeu(perdeu_out),
        .timeout(timeout_out),
        .pronto(pronto_out),
        .leds(leds_out),
        .db_clock(db_clock_out),
        .db_tem_jogada(db_tem_jogada_out),
        .db_chavesIgualMemoria(db_chavesIgualMemoria_out),
        .db_enderecoIgualSequencia(db_enderecoIgualSequencia_out),
        .db_fimS(db_fimS_out),
        .db_contagem(db_contagem_out),
        .db_memoria(db_memoria_out),
        .db_jogadafeita(db_jogadafeita_out),
        .db_sequencia(db_sequencia_out),
        .db_estado(db_estado_out),
        .db_timeout(db_timeout_out),
        .db_timeoutL(db_timeoutL_out),
        .db_seletor_memoria(db_seletor_memoria_out)
    );

    // Gabarito
    reg [3:0] jogadas_caso1[0:15];
    reg [3:0] jogadas_caso2[0:15];

    initial begin
        jogadas_caso1[0] = 4'b0001;
        jogadas_caso1[1] = 4'b0010;
        jogadas_caso1[2] = 4'b0100;
        jogadas_caso1[3] = 4'b1000;
        jogadas_caso1[4] = 4'b0100;
        jogadas_caso1[5] = 4'b0010;
        jogadas_caso1[6] = 4'b0001;
        jogadas_caso1[7] = 4'b0001;
        jogadas_caso1[8] = 4'b0010;
        jogadas_caso1[9] = 4'b0010;
        jogadas_caso1[10] = 4'b0100;
        jogadas_caso1[11] = 4'b0100;
        jogadas_caso1[12] = 4'b1000;
        jogadas_caso1[13] = 4'b1000;
        jogadas_caso1[14] = 4'b0001;
        jogadas_caso1[15] = 4'b0100;
    end

    initial begin
        jogadas_caso2[0] = 4'b0001;
        jogadas_caso2[1] = 4'b0001;
        jogadas_caso2[2] = 4'b0001;
        jogadas_caso2[3] = 4'b0001;
        jogadas_caso2[4] = 4'b0010;
        jogadas_caso2[5] = 4'b0010;
        jogadas_caso2[6] = 4'b0010;
        jogadas_caso2[7] = 4'b0010;
        jogadas_caso2[8] = 4'b0100;
        jogadas_caso2[9] = 4'b0100;
        jogadas_caso2[10] = 4'b0100;
        jogadas_caso2[11] = 4'b0100;
        jogadas_caso2[12] = 4'b1000;
        jogadas_caso2[13] = 4'b1000;
        jogadas_caso2[14] = 4'b1000;
        jogadas_caso2[15] = 4'b1000;
    end

    // Variáveis de loop
    integer i, j;

    // Geração dos estímulos de entrada
    initial begin
        $display("Inicio da simulacao");

        // Condições iniciais
        caso = 0;
        clock_in = 1;
        reset_in = 0;
        jogar_in = 0;
        botoes_in = 4'b0000;
        #(clockPeriod);

        // Teste 1: Reset do circuito
        caso = 1;
        @(negedge clock_in);
        reset_in = 1;
        #(clockPeriod);
        reset_in = 0;
        #(10 * clockPeriod);

        // Teste 2: Jogar por 5 períodos de clock
        caso = 2;
        #(2 * clockPeriod);
        jogar_in = 1;
        #(5 * clockPeriod);
        jogar_in = 0;
        #(10 * clockPeriod);

        // Testes de jogadas
        for (i = 3; i <= 18; i = i + 1) begin
            #(1_000_000 * (i - 2));
            #(500_000);
            caso = i;
            @(negedge clock_in);

            for (j = 0; j < i-2; j = j + 1) begin
                botoes_in = jogadas_caso1[j];
                #(10 * clockPeriod);
                botoes_in = 4'b0000;
                #(10 * clockPeriod);
            end
        end

        // Teste 2: Jogar por 5 períodos de clock
        caso = 2;
        #(2 * clockPeriod);
        memoria_in = 1;
        #(2 * clockPeriod);
        jogar_in = 1;
        #(5 * clockPeriod);
        jogar_in = 0;
        #(10 * clockPeriod);

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*/
