// Digital circuit playseq_jogo.dig as structural Verilog
module playseq_jogo (
  input  CLOCK,
  input  [1:0] Memoria_a_ser_Jogada,
  input  [1:0] Nivel_de_Dificuldade,
  output [6:0] CONTAGEM,
  output [6:0] SEQUENCIA,
  output [6:0] ESTADO,
  output [6:0] MEMORIA,
  output [6:0] JOGADA_FEITA,
  output PRONTO,
  output C__eq__M,
  output E__eq__S,
  output db__clock,
  output db__tem__jogada,
  output db__fimS,
  output db__seletor__memoria,
  output db__timeout,
  output db__timeoutL
);

  wire JOGAR_out, RESET_out, u_jogo_playseq_ganhou, u_jogo_playseq_perdeu, u_jogo_playseq_timeout;
  wire [3:0] BOTOES_0_p1, u_jogo_playseq_leds;
  wire [7:0] not_1_out, not_2_out, not_3_out, not_4_out, not_5_out;

  Button RESET (.out(RESET_out));
  Button JOGAR (.out(JOGAR_out));
  // ButtonLED BOTOES_0: pin names not known; wires that end beside it: BOTOES_0_p1[0], 1'b1
  // ButtonLED BOTOES_1: pin names not known; wires that end beside it: BOTOES_0_p1[1], 1'b1
  // ButtonLED BOTOES_2: pin names not known; wires that end beside it: BOTOES_0_p1[2], 1'b1
  jogo_playseq #(.applicationType("IVERILOG"), .iverilogOptions("-I \"/home/baunilha/Repositories/PCS3635/experiment_06/deasafio_exp6/\"")) u_jogo_playseq (
    .clock(CLOCK), .reset(RESET_out), .jogar(JOGAR_out), .botoes(BOTOES_0_p1),
    .memoria(Memoria_a_ser_Jogada), .nivel(Nivel_de_Dificuldade), .ganhou(u_jogo_playseq_ganhou),
    .perdeu(u_jogo_playseq_perdeu), .timeout(u_jogo_playseq_timeout), .pronto(PRONTO),
    .leds(u_jogo_playseq_leds), .db_clock(db__clock), .db_tem_jogada(db__tem__jogada),
    .db_chavesIgualMemoria(C__eq__M), .db_enderecoIgualSequencia(E__eq__S), .db_fimS(db__fimS),
    .db_contagem(CONTAGEM), .db_memoria(MEMORIA), .db_jogadafeita(JOGADA_FEITA), .db_sequencia(SEQUENCIA),
    .db_estado(ESTADO), .db_seletor_memoria(db__seletor__memoria), .db_timeout(db__timeout),
    .db_timeoutL(db__timeoutL));
  // ButtonLED BOTOES_3: pin names not known; wires that end beside it: BOTOES_0_p1[3], 1'b1
  LED LEDS_0 (.in(u_jogo_playseq_leds[0]));
  LED LEDS_1 (.in(u_jogo_playseq_leds[1]));
  LED LEDS_2 (.in(u_jogo_playseq_leds[2]));
  LED LEDS_3 (.in(u_jogo_playseq_leds[3]));
  assign not_1_out = ~{1'b0, CONTAGEM};  // Not not_1, 8 bits wide
  assign not_2_out = ~{1'b0, JOGADA_FEITA};  // Not not_2, 8 bits wide
  LED GANHOU (.in(u_jogo_playseq_ganhou));
  LED PERDEU (.in(u_jogo_playseq_perdeu));
  LED TIMEOUT (.in(u_jogo_playseq_timeout));
  Seven_Seg seven_seg_1 (
    .a(not_1_out[0]), .b(not_1_out[1]), .c(not_1_out[2]), .d(not_1_out[3]), .e(not_1_out[4]),
    .f(not_1_out[5]), .g(not_1_out[6]), .dp(not_1_out[7]));
  Seven_Seg seven_seg_2 (
    .a(not_2_out[0]), .b(not_2_out[1]), .c(not_2_out[2]), .d(not_2_out[3]), .e(not_2_out[4]),
    .f(not_2_out[5]), .g(not_2_out[6]), .dp(not_2_out[7]));
  assign not_3_out = ~{1'b0, MEMORIA};  // Not not_3, 8 bits wide
  assign not_4_out = ~{1'b0, SEQUENCIA};  // Not not_4, 8 bits wide
  assign not_5_out = ~{1'b0, ESTADO};  // Not not_5, 8 bits wide
  Seven_Seg seven_seg_3 (
    .a(not_3_out[0]), .b(not_3_out[1]), .c(not_3_out[2]), .d(not_3_out[3]), .e(not_3_out[4]),
    .f(not_3_out[5]), .g(not_3_out[6]), .dp(not_3_out[7]));
  Seven_Seg seven_seg_4 (
    .a(not_4_out[0]), .b(not_4_out[1]), .c(not_4_out[2]), .d(not_4_out[3]), .e(not_4_out[4]),
    .f(not_4_out[5]), .g(not_4_out[6]), .dp(not_4_out[7]));
  Seven_Seg seven_seg_5 (
    .a(not_5_out[0]), .b(not_5_out[1]), .c(not_5_out[2]), .d(not_5_out[3]), .e(not_5_out[4]),
    .f(not_5_out[5]), .g(not_5_out[6]), .dp(not_5_out[7]));

  // Notes on the sheet:
  //   CLOCK: Hz: 1000
  //   Nivel_de_Dificuldade: default 1
endmodule

/* Code of jogo_playseq:
//------------------------------------------------------------------
// Arquivo   : jogo_playseq.v
// Projeto   : PlaySeq
//------------------------------------------------------------------
// Descricao : Circuito principal do jogo PlaySeq
//             
//------------------------------------------------------------------
// Revisoes  :
//     Data        Versao  Autor             Descricao
//     07/03/2025  1.0     Ana Vitória       versao inicial
//------------------------------------------------------------------
//
module jogo_playseq (
    input clock,
    input reset,
    input jogar,
    input [3:0] botoes,
    input [1:0] memoria,
    input [1:0] nivel,
    output ganhou,
    output perdeu,
    output timeout,
    output pronto,
    output [3:0] leds,
    output db_clock,
    output db_tem_jogada,
    output db_chavesIgualMemoria,
    output db_enderecoIgualSequencia,
    output db_fimS,
    output [6:0] db_contagem,
    output [6:0] db_memoria,
    output [6:0] db_jogadafeita,
    output [6:0] db_sequencia,
    output [6:0] db_estado,
    output db_seletor_memoria,
    // Nossos debugs
    output db_timeout,
    output db_timeoutL
);

    wire [3:0] s_jogadafeita;
    wire [3:0] s_contagem;
    wire [3:0] s_memoria;
    wire [3:0] s_estado;
    wire [3:0] s_sequencia;
    wire s_tem_jogada;
    wire s_fimE;
    wire s_fimS;
    wire s_igualE;
    wire s_fim_timeout;
    wire s_contaT;
    wire s_contaS;
    wire s_zeraS;
    wire s_contaE;
    wire s_zeraE;
    wire s_igualS;
    wire s_zeraR;
    wire s_registraR;
    wire [1:0] s_nivel_uc;
    wire s_zeraT;
    wire s_timeoutL;
    wire s_menorS;
    wire s_controla_leds;
    wire s_zeraT_leds;
    wire s_contaT_leds;
    wire s_fase_preview;
    wire [1:0] s_memoria_uc;
    wire s_carregaE;
    wire s_pare;
    wire s_contaJ;
    wire s_zeraJ;

    // Fluxo de Dados
    playseq_fluxo_dados FD (
        .clock                     ( clock              ),
        .botoes                    ( botoes             ),
        .nivel                     ( s_nivel_uc         ),
        .zeraT                     ( s_zeraT            ),
        .zeraR                     ( s_zeraR            ),
        .registraR                 ( s_registraR        ),
        .contaE                    ( s_contaE           ),
        .contaS                    ( s_contaS           ),
        .contaT                    ( s_contaT           ),
        .contaJ                    ( s_contaJ           ),
        .zeraE                     ( s_zeraE            ),
        .zeraS                     ( s_zeraS            ),
        .zeraJ                     ( s_zeraJ            ),
        .carregaE                  ( s_carregaE         ),
        .controla_leds             ( s_controla_leds    ),
        .zeraT_leds                ( s_zeraT_leds       ),
        .contaT_leds               ( s_contaT_leds      ),
        .fase_preview              ( s_fase_preview     ),
        .seletor_memoria           ( s_memoria_uc       ),
        .igual                     ( s_igualE           ),
        .enderecoIgualSequencia    ( s_igualS           ),
        .fimE                      ( s_fimE             ),
        .fimS                      ( s_fimS             ),
        .db_contagem               ( s_contagem         ),
        .db_jogadafeita            ( s_jogadafeita      ),
        .db_memoria                ( s_memoria          ),
        .tem_jogada                ( s_tem_jogada       ),
        .controle_timeout          ( s_fim_timeout      ),
        .db_sequencia              ( s_sequencia        ),
        .controle_timeout_led      ( s_timeoutL         ),
        .sequenciaMenorQueEndereco ( s_menorS           ),
        .leds                      ( leds               ),
        .db_seletor_memoria        ( db_seletor_memoria ),
        .pare                      ( s_pare             )
    );

    // Unidade de Controle
    playseq_unidade_controle UC (
        .clock         ( clock          ),
        .reset         ( reset          ),
        .jogar         ( jogar          ),
        .nivel         ( nivel          ),
        .fimE          ( s_fimE         ),
        .igualE        ( s_igualE       ),
        .igualS        ( s_igualS       ),
        .tem_jogada    ( s_tem_jogada   ),
        .timeout       ( s_fim_timeout  ),
        .timeoutL      ( s_timeoutL     ),
        .menorS        ( s_menorS       ),
        .memoria       ( memoria        ),
        .pare          ( s_pare         ),
        .zeraE         ( s_zeraE        ),
        .contaE        ( s_contaE       ),
        .carregaE      ( s_carregaE     ),
        .zeraS         ( s_zeraS        ),
        .contaS        ( s_contaS       ),
        .zeraR         ( s_zeraR        ),
        .registraR     ( s_registraR    ),
        .zeraJ         ( s_zeraJ        ),
        .contaJ        ( s_contaJ       ),
        .ganhou        ( ganhou         ),
        .perdeu        ( perdeu         ),
        .pronto        ( pronto         ),
        .db_estado     ( s_estado       ),
        .deu_timeout   ( timeout        ),
        .contaT        ( s_contaT       ),
        .nivel_uc      ( s_nivel_uc     ),
        .zeraT         ( s_zeraT        ),
        .controla_leds ( s_controla_leds),
        .zeraT_leds    ( s_zeraT_leds   ),
        .contaT_leds   ( s_contaT_leds  ),
        .fase_preview  ( s_fase_preview ),
        .memoria_uc    ( s_memoria_uc   )
    );

    // Display das botoes
    hexa7seg HEX2 (
        .hexa    ( s_jogadafeita  ),
        .display ( db_jogadafeita )
    );

    // Display dos endereços codificados
    hexa7seg HEX0 (
        .hexa    ( s_contagem  ),
        .display ( db_contagem )
    );

    // Display do conteúdo em uma posição de memória
    hexa7seg HEX1 (
        .hexa    ( s_memoria  ),
        .display ( db_memoria )
    );

    // Display do estado atual
    hexa7seg HEX5 (
        .hexa    ( s_estado  ),
        .display ( db_estado )
    );

    // Display da sequência atual
    hexa7seg HEX3 (
        .hexa    ( s_sequencia  ),
        .display ( db_sequencia )
    );

assign db_chavesIgualMemoria = s_igualE;
assign db_enderecoIgualSequencia = s_igualS;
assign db_fimS = s_fimS;
assign db_tem_jogada = s_tem_jogada;
assign db_clock = clock;
assign db_timeout = s_fim_timeout;
assign db_timeoutL = s_timeoutL;
endmodule


/* -----------------------------------------------------------------
 *  Arquivo   : comparador_85.v
 *  Projeto   : PlaySeq
 * -----------------------------------------------------------------
 * Descricao : comparador de magnitude de 4 bits 
 *             similar ao CI 7485
 *             baseado em descricao comportamental disponivel em	
 * https://web.eecs.umich.edu/~jhayes/iscas.restore/74L85b.v
 * -----------------------------------------------------------------
 * Revisoes  :
 *     Data        Versao  Autor             Descricao
 *     21/12/2023  1.0     Edson Midorikawa  criacao
 * -----------------------------------------------------------------
 * /

module comparador_85 (ALBi, AGBi, AEBi, A, B, ALBo, AGBo, AEBo);

    input[3:0] A, B;
    input      ALBi, AGBi, AEBi;
    output     ALBo, AGBo, AEBo;
    wire[4:0]  CSL, CSG;

    assign CSL  = ~A + B + ALBi;
    assign ALBo = ~CSL[4];
    assign CSG  = A + ~B + AGBi;
    assign AGBo = ~CSG[4];
    assign AEBo = ((A == B) && AEBi);

endmodule /* comparador_85 * /

//------------------------------------------------------------------
// Arquivo   : contador_163.v
// Projeto   : PlaySeq
//------------------------------------------------------------------
// Descricao : Contador binario de 4 bits, modulo 16
//             similar ao componente 74163
//
// baseado no componente Vrcntr4u.v do livro Digital Design Principles 
// and Practices, Fifth Edition, by John F. Wakerly              
//------------------------------------------------------------------
// Revisoes  :
//     Data        Versao  Autor             Descricao
//     14/12/2023  1.0     Edson Midorikawa  versao inicial
//------------------------------------------------------------------
//
module contador_163 ( clock, clr, ld, ent, enp, D, Q, rco );
    input clock, clr, ld, ent, enp;
    input [3:0] D;
    output reg [3:0] Q;
    output reg rco;

    always @ (posedge clock)
        if (~clr)               Q <= 4'd0;
        else if (~ld)           Q <= D;
        else if (ent && enp)    Q <= Q + 1'b1;
        else                    Q <= Q;
 
    always @ (Q or ent)
        if (ent && (Q == 4'd15))   rco = 1;
        else                       rco = 0;
endmodule


/*---------------Laboratorio Digital-------------------------------------
 * Arquivo   : contador_m.v
 * Projeto   : PlaySeq
 *-----------------------------------------------------------------------
 * Descricao : contador binario, modulo m, com parametros 
 *             M (modulo do contador) e N (numero de bits),
 *             sinais para clear assincrono (zera_as) e sincrono (zera_s)
 *             e saidas de fim e meio de contagem
 *             
 *-----------------------------------------------------------------------
 * Revisoes  :
 *     Data        Versao  Autor             Descricao
 *     30/01/2024  1.0     Edson Midorikawa  criacao
 *     16/01/2025  1.1     Edson Midorikawa  revisao
 *-----------------------------------------------------------------------
 * /

module contador_m #(parameter M=100, N=7)
  (
   input  wire          clock,
   input  wire          zera_as,
   input  wire          zera_s,
   input  wire          conta,
   output reg  [N-1:0]  Q,
   output reg           fim,
   output reg           meio
  );

  always @(posedge clock or posedge zera_as) begin
    if (zera_as) begin
      Q <= 0;
    end else if (clock) begin
      if (zera_s) begin
        Q <= 0;
      end else if (conta) begin
        if (Q == M-1) begin
          Q <= 0;
        end else begin
          Q <= Q + 1'b1;
        end
      end
    end
  end

  // Saidas
  always @ (Q)
      if (Q == M-1)   fim = 1;
      else            fim = 0;

  always @ (Q)
      if (Q == M/2-1) meio = 1;
      else             meio = 0;

endmodule

/* ------------------------------------------------------------------------
 *  Arquivo   : edge_detector.v
 *  Projeto   : PlaySeq
 * ------------------------------------------------------------------------
 *  Descricao : detector de borda
 *              gera um pulso na saida de 1 periodo de clock
 *              a partir da detecao da borda de subida sa entrada
 *
 *              sinal de reset ativo em alto
 *
 *              > codigo adaptado a partir de codigo VHDL disponivel em
 *                https://surf-vhdl.com/how-to-design-a-good-edge-detector/
 * ------------------------------------------------------------------------
 *  Revisoes  :
 *      Data        Versao  Autor             Descricao
 *      26/01/2024  1.0     Edson Midorikawa  versao inicial
 * ------------------------------------------------------------------------
 * /

module edge_detector (
    input  clock,
    input  reset,
    input  sinal,
    output pulso
);

    reg reg0;
    reg reg1;

    always @(posedge clock or posedge reset) begin
        if (reset) begin
            reg0 <= 1'b0;
            reg1 <= 1'b0;
        end else if (clock) begin
            reg0 <= sinal;
            reg1 <= reg0;
        end
    end

    assign pulso = ~reg1 & reg0;

endmodule

/* ----------------------------------------------------------------
 * Arquivo   : hexa7seg.v
 * Projeto   : PlaySeq
 *--------------------------------------------------------------
 * Descricao : decodificador hexadecimal para 
 *             display de 7 segmentos 
 * 
 * entrada : hexa - codigo binario de 4 bits hexadecimal
 * saida   : sseg - codigo de 7 bits para display de 7 segmentos
 *
 * baseado no componente bcd7seg.v da Intel FPGA
 *--------------------------------------------------------------
 * dica de uso: mapeamento para displays da placa DE0-CV
 *              bit 6 mais significativo é o bit a esquerda
 *              p.ex. sseg(6) -> HEX0[6] ou HEX06
 *--------------------------------------------------------------
 * Revisoes  :
 *     Data        Versao  Autor             Descricao
 *     24/12/2023  1.0     Edson Midorikawa  criacao
 *--------------------------------------------------------------
 * /

module hexa7seg (hexa, display);
    input      [3:0] hexa;
    output reg [6:0] display;

    /*
     *    ---
     *   | 0 |
     * 5 |   | 1
     *   |   |
     *    ---
     *   | 6 |
     * 4 |   | 2
     *   |   |
     *    ---
     *     3
     * /
        
    always @(hexa)
    case (hexa)
        4'h0:    display = 7'b1000000;
        4'h1:    display = 7'b1111001;
        4'h2:    display = 7'b0100100;
        4'h3:    display = 7'b0110000;
        4'h4:    display = 7'b0011001;
        4'h5:    display = 7'b0010010;
        4'h6:    display = 7'b0000010;
        4'h7:    display = 7'b1111000;
        4'h8:    display = 7'b0000000;
        4'h9:    display = 7'b0010000;
        4'ha:    display = 7'b0001000;
        4'hb:    display = 7'b0000011;
        4'hc:    display = 7'b1000110;
        4'hd:    display = 7'b0100001;
        4'he:    display = 7'b0000110;
        4'hf:    display = 7'b0001110;
        default: display = 7'b1111111;
    endcase
endmodule

//------------------------------------------------------------------
// Arquivo   : memoria_2.v
// Projeto   : PlaySeq
//------------------------------------------------------------------
// Descricao : ROM sincrona 16x4 (conteúdo pre-programado)
//             
//------------------------------------------------------------------
// Revisoes  :
//     Data        Versao  Autor             Descricao
//     14/12/2023  1.0     Edson Midorikawa  versao inicial
//------------------------------------------------------------------
//
module memoria_2 (clock, address, data_out);
    input            clock;
    input      [3:0] address;
    output reg [3:0] data_out;

    always @ (posedge clock)
    begin
        case (address)
            4'b0000: data_out = 4'b0001;
            4'b0001: data_out = 4'b0010;
            4'b0010: data_out = 4'b1000;
            4'b0011: data_out = 4'b0100;
            4'b0100: data_out = 4'b0010;
            4'b0101: data_out = 4'b1000;
            4'b0110: data_out = 4'b0001;
            4'b0111: data_out = 4'b0100;
            4'b1000: data_out = 4'b1000;
            4'b1001: data_out = 4'b0001;
            4'b1010: data_out = 4'b0100;
            4'b1011: data_out = 4'b0010;
            4'b1100: data_out = 4'b0001;
            4'b1101: data_out = 4'b0010;
            4'b1110: data_out = 4'b1000;
            4'b1111: data_out = 4'b0100;
        endcase
    end
endmodule

//------------------------------------------------------------------
// Arquivo   : memoria_1.v
// Projeto   : PlaySeq
//------------------------------------------------------------------
// Descricao : ROM sincrona 16x4 (conteúdo pre-programado)
//             
//------------------------------------------------------------------
// Revisoes  :
//     Data        Versao  Autor             Descricao
//     14/12/2023  1.0     Edson Midorikawa  versao inicial
//------------------------------------------------------------------
//
module memoria_1 (clock, address, data_out);
    input            clock;
    input      [3:0] address;
    output reg [3:0] data_out;

    always @ (posedge clock)
    begin
        case (address)
            4'b0000: data_out = 4'b0001; // 4
            4'b0001: data_out = 4'b0001; // 5
            4'b0010: data_out = 4'b0010; // 6
            4'b0011: data_out = 4'b0010; // 7 
            4'b0100: data_out = 4'b0100; // 8
            4'b0101: data_out = 4'b0100; // 9
            4'b0110: data_out = 4'b1000; // 10
            4'b0111: data_out = 4'b1000; // 11
            4'b1000: data_out = 4'b0100; // 12
            4'b1001: data_out = 4'b0100; // 13
            4'b1010: data_out = 4'b0010; // 14
            4'b1011: data_out = 4'b0010; // 15
            4'b1100: data_out = 4'b0001; // 16
            4'b1101: data_out = 4'b0001; // 17
            4'b1110: data_out = 4'b0010; // 18
            4'b1111: data_out = 4'b0010; // 19
        endcase
    end
endmodule

//------------------------------------------------------------------
// Arquivo   : memoria_3.v
// Projeto   : PlaySeq
//------------------------------------------------------------------
// Descricao : ROM sincrona 16x4 (conteúdo pre-programado)
//             
//------------------------------------------------------------------
// Revisoes  :
//     Data        Versao  Autor             Descricao
//     14/12/2023  1.0     Edson Midorikawa  versao inicial
//------------------------------------------------------------------
//
module memoria_3 (clock, address, data_out);
    input            clock;
    input      [3:0] address;
    output reg [3:0] data_out;

    always @ (posedge clock)
    begin
        case (address)
            4'b0000: data_out = 4'b0001;
            4'b0001: data_out = 4'b0010;
            4'b0010: data_out = 4'b1000;
            4'b0011: data_out = 4'b0100;
            4'b0100: data_out = 4'b0100;
            4'b0101: data_out = 4'b1000;
            4'b0110: data_out = 4'b0010;
            4'b0111: data_out = 4'b0001;
            4'b1000: data_out = 4'b0001;
            4'b1001: data_out = 4'b0010;
            4'b1010: data_out = 4'b1000;
            4'b1011: data_out = 4'b0100;
            4'b1100: data_out = 4'b0100;
            4'b1101: data_out = 4'b1000;
            4'b1110: data_out = 4'b0010;
            4'b1111: data_out = 4'b0001;
        endcase
    end
endmodule

/*------------------------------------------------------------------------
 * Arquivo   : mux2x1_n.v
 * Projeto   : PlaySeq
 *------------------------------------------------------------------------
 * Descricao : multiplexador 2x1 com entradas de n bits (parametrizado) 
 * 
 * adaptado a partir do codigo my_4t1_mux.vhd do livro "Free Range VHDL"
 * 
 * exemplo de uso: ver testbench mux2x1_n_tb.v
 *------------------------------------------------------------------------
 * Revisoes  :
 *     Data        Versao  Autor             Descricao
 *     15/02/2024  1.0     Edson Midorikawa  criacao
 *------------------------------------------------------------------------
 * /

module mux2x1_n #(
    parameter BITS = 4
) (
    input      [BITS-1:0] D0,
    input      [BITS-1:0] D1,
    input                 SEL,
    output reg [BITS-1:0] OUT
);

always @(*) begin
    case (SEL)
        1'b0:    OUT = D0;
        1'b1:    OUT = D1;
        default: OUT = {BITS{1'b1}}; // todos os bits em 1
    endcase
end

endmodule

/*------------------------------------------------------------------------
 * Arquivo   : mux2x1.v
 * Projeto   : PlaySeq
 *------------------------------------------------------------------------
 * Descricao : multiplexador 2x1
 * 
 * adaptado a partir do codigo my_4t1_mux.vhd do livro "Free Range VHDL"
 * 
 * exemplo de uso: ver testbench mux2x1_tb.v
 *------------------------------------------------------------------------
 * Revisoes  :
 *     Data        Versao  Autor             Descricao
 *     15/02/2024  1.0     Edson Midorikawa  criacao
 *     31/01/2025  1.1     Edson Midorikawa  revisao
 *------------------------------------------------------------------------
 * /

module mux2x1 (
    input      D0,
    input      D1,
    input      SEL,
    output reg OUT
);

always @(*) begin
    case (SEL)
        1'b0:    OUT = D0;
        1'b1:    OUT = D1;
        default: OUT = 0; // saida em 0
    endcase
end

endmodule

/*------------------------------------------------------------------------
 * Arquivo   : mux4x2_n.v
 * Projeto   : PlaySeq
 *------------------------------------------------------------------------
 * Descricao : multiplexador 4x(2 bit de seletor) com entradas de n bits 
 * (parametrizado) 
 * 
 *------------------------------------------------------------------------
 * Revisoes  :
 *     Data        Versao  Autor             Descricao
 *     07/03/2024  1.0     Ana Vitória       criacao
 *------------------------------------------------------------------------
 * /

module mux4x2_n #(
    parameter BITS = 4
) (
    input      [BITS-1:0] D0,
    input      [BITS-1:0] D1,
    input      [BITS-1:0] D2,
    input      [BITS-1:0] D3,
    input      [1:0]      SEL,
    output reg [BITS-1:0] OUT
);

always @(*) begin
    case (SEL)
        2'b00:    OUT = D0;
        2'b01:    OUT = D1;
        2'b10:    OUT = D2;
        2'b11:    OUT = D3;
        default: OUT = {BITS{1'b1}}; // todos os bits em 1
    endcase
end

endmodule

//------------------------------------------------------------------
// Arquivo   : playseq_fluxo_dados.v
// Projeto   : PlaySeq
//------------------------------------------------------------------
// Descricao : Fluxo de Dados do Jogo PlaySeq
//             
//------------------------------------------------------------------
// Revisoes  :
//     Data        Versao  Autor             Descricao
//     07/03/2025  1.0     Ana Vitória       versao inicial
//------------------------------------------------------------------
//

module playseq_fluxo_dados (
    input clock,
    input [3:0] botoes,
    input [1:0] nivel,
    input zeraT,
    input zeraR,
    input registraR,
    input contaE,
    input contaS,
    input contaT,
    input contaJ,
    input zeraE,
    input zeraS,
    input zeraJ,
    input carregaE,
    input controla_leds,
    input zeraT_leds,
    input contaT_leds,
    input fase_preview,
    input [1:0] seletor_memoria,
    output igual,
    output enderecoIgualSequencia,
    output fimE,
    output fimS,
    output tem_jogada,
    output [3:0] db_contagem,
    output [3:0] db_jogadafeita,
    output [3:0] db_memoria,
    output controle_timeout,
    output [3:0] db_sequencia,
    output controle_timeout_led,
    output sequenciaMenorQueEndereco,
    output [3:0] leds,
    output db_seletor_memoria,
    output pare
);

    wire [3:0] s_endereco;
    wire [3:0] s_dado;
    wire [3:0] s_botoes;
    wire [3:0] s_sequencia;
    wire [3:0] s_sequencia_fixo;
    wire s_tem_jogada = |botoes;
    wire [3:0] s_mux;
    wire [3:0] s_mem1;
    wire [3:0] s_mem2;
    wire [3:0] s_mem3;
    wire [1:0] s_contagem;
    wire [3:0] s_quant_inicial;
    wire [3:0] s_seletor_final = {nivel, seletor_memoria};

    // dificuldade_quant
    mux4x2_n #( .BITS(1) ) mux (
        .D0 (~s_contagem[0] & ~s_contagem[1]),
        .D1 (s_contagem[0] & ~s_contagem[1]),
        .D2 (~s_contagem[0] & s_contagem[1]),
        .D3 (1'b1),
        .SEL (nivel),
        .OUT (pare)
    );

    // decide o início para cada situação, sempre defasado de 1
    mux12x4_n #( .BITS(4) ) mux_inicial (
        .D0 (4'b0100), // feito
        .D1 (4'b1000), // feito
        .D2 (4'b0111), // feito
        .D3 (4'b0100),
        .D4 (4'b0101), //feito
        .D5 (4'b1000), // feito
        .D6 (4'b0101), // feito
        .D7 (4'b0100),
        .D8 (4'b0100), // feito
        .D9 (4'b1000), // feito
        .D10(4'b0011), // feito
        .D11(4'b0100),
        .SEL (s_seletor_final),
        .OUT (s_quant_inicial)
    );

    // decide o final para cada situação
    mux12x4_n #( .BITS(1) ) mux_final (
        .D0 (s_endereco[0] & s_endereco[1] & s_endereco[2] & s_endereco[3]), // feito
        .D1 (s_endereco[0] & s_endereco[1] & s_endereco[2] & s_endereco[3]), // feito
        .D2 (~s_endereco[0] & s_endereco[1] & s_endereco[2] & s_endereco[3]), // feito
        .D3 (s_endereco[0] & s_endereco[1] & s_endereco[2] & s_endereco[3]),
        .D4 (s_endereco[0] & s_endereco[1] & s_endereco[2] & s_endereco[3]), // feito
        .D5 (s_endereco[0] & s_endereco[1] & s_endereco[2] & s_endereco[3]), // feito
        .D6 (s_endereco[0] & s_endereco[1] & s_endereco[2] & s_endereco[3]), // feito
        .D7 (s_endereco[0] & s_endereco[1] & s_endereco[2] & s_endereco[3]),
        .D8 (s_endereco[0] & s_endereco[1] & s_endereco[2] & s_endereco[3]), // feito
        .D9 (s_endereco[0] & s_endereco[1] & s_endereco[2] & s_endereco[3]), // feito
        .D10(~s_endereco[0] & s_endereco[1] & s_endereco[2] & s_endereco[3]), // feito
        .D11(s_endereco[0] & s_endereco[1] & s_endereco[2] & s_endereco[3]),
        .SEL (s_seletor_final),
        .OUT (fimE)
    );

    // mux n
    mux2x1_n #( .BITS(4) ) mux_leds (
      .D0(botoes),
      .D1(s_mux),
      .SEL(fase_preview),
      .OUT(leds)
    );

    // mux n
    mux2x1_n #( .BITS(4) ) mux_zera (
      .D0(4'b0000),
      .D1(s_dado),
      .SEL(controla_leds),
      .OUT(s_mux)
    );

    // contador endereços
    contador_163 contEnd (
        .clock (clock),
        .clr   (~zeraE),
        .ld    (1'b1),
        .ent   (1'b1),
        .enp   (contaE),
        .D     (4'b0),
        .Q     (s_endereco),
        .rco   ()
    );

    // contador sequencias
    contador_163 contLmt (
        .clock (clock),
        .clr   (~zeraS),
        .ld    (~carregaE),
        .ent   (1'b1),
        .enp   (contaS),
        .D     (s_quant_inicial),
        .Q     (s_sequencia),
        .rco   (fimS)
    );

    // comparador jogadas
    comparador_85 compJog (
        .A    (s_dado),
        .B    (s_botoes),
        .ALBi (1'b0),
        .AGBi (1'b0),
        .AEBi (1'b1),
        .ALBo (),
        .AGBo (),
        .AEBo (igual)
    );

    // comparador sequencias
    comparador_85 compLmt (
        .A    (s_sequencia),
        .B    (s_endereco),
        .ALBi (1'b0),
        .AGBi (1'b0),
        .AEBi (1'b1),
        .ALBo (sequenciaMenorQueEndereco),
        .AGBo (),
        .AEBo (enderecoIgualSequencia)
    );

    // dificuldade_seq
    mux4x2_n #( .BITS(4) ) mux_jogo (
      .D0(s_mem1),
      .D1(s_mem2),
      .D2(s_mem3),
      .D3(s_mem1), // será memória personalizável mais para frente
      .SEL(seletor_memoria),
      .OUT(s_dado)
    );

    // memória 1
    memoria_1 memoria1 (
        .clock    (clock),
        .address  (s_endereco),
        .data_out (s_mem1)
    );

    // memória 2
    memoria_2 memoria2 (
        .clock    (clock),
        .address  (s_endereco),
        .data_out (s_mem2)
    );

    // memória 3
    memoria_3 memoria3 (
        .clock    (clock),
        .address  (s_endereco),
        .data_out (s_mem3)
    );

    // registrador
    registrador_4 regBotoes (
        .clock  (clock),
        .clear  (zeraR),
        .enable (registraR),
        .D      (botoes),
        .Q      (s_botoes)
    );

    edge_detector detector (
        .clock (clock),
        .reset (zeraS),
        .sinal (s_tem_jogada),
        .pulso (tem_jogada)
    );

    contador_m #(.M(5000), .N(13)) contador_timeout_jogadas (
        .clock   (clock),
        .zera_as (zeraC || zeraR),
        .zera_s  (zeraT),
        .conta   (contaT),
        .Q       (),
        .fim     (controle_timeout),
        .meio    ()
    );

    contador_m #(.M(500), .N(9)) contador_timeout_leds (
        .clock   (clock),
        .zera_as (zeraC || zeraR),
        .zera_s  (zeraT_leds),
        .conta   (contaT_leds),
        .Q       (),
        .fim     (controle_timeout_led),
        .meio    ()
    );

    contador_m #(.M(4), .N(2)) contador_jogadas (
        .clock   (clock),
        .zera_as (zeraC || zeraR), // precisa ser um zera diferente
        .zera_s  (zeraJ),
        .conta   (contaJ), // precisa ser um zera diferente
        .Q       (s_contagem),
        .fim     (),
        .meio    ()
    );

    assign db_memoria  = s_dado;
    assign db_contagem = s_endereco;
    assign db_sequencia = s_sequencia;
    assign db_jogadafeita = s_botoes;
    assign db_seletor_memoria = seletor_memoria;
endmodule

//------------------------------------------------------------------
// Arquivo   : playseq_unidade_controle.v
// Projeto   : PlaySeq
//------------------------------------------------------------------
// Descricao : Unidade de controle do Jogo PlaySeq
//         
//------------------------------------------------------------------
// Revisoes  :
//     Data        Versao  Autor         Descricao
//     07/03/2024  1.0     Ana Vitória   versao inicial
//------------------------------------------------------------------
//

module playseq_unidade_controle (
    input clock,
    input reset,
    input jogar,
    input [1:0] nivel,
    input fimE,
    input igualE,
    input igualS,
    input tem_jogada,
    input timeout,
    input timeoutL,
    input menorS,
    input [1:0] memoria,
    input pare,
    output reg zeraE,
    output reg contaE,
    output reg carregaE,
    output reg zeraS,
    output reg contaS,
    output reg zeraR,
    output reg registraR,
    output reg zeraJ,
    output reg contaJ,
    output reg ganhou,
    output reg perdeu,
    output reg pronto,
    output reg [3:0] db_estado,
    output reg deu_timeout,
    output reg contaT,
    output reg [1:0] nivel_uc,
    output reg zeraT,
    output reg controla_leds,
    output reg zeraT_leds,
    output reg contaT_leds,
    output reg fase_preview,
    output reg [1:0] memoria_uc
);

    // Define estados
    parameter inicial        = 4'b0000;  // 0
    parameter preparacao     = 4'b0001;  // 1
    parameter nova_seq       = 4'b0010;  // 2
    parameter mostra_leds    = 4'b1011;  // B
    parameter mostrou_led    = 4'b1100;  // C
    parameter espera_led     = 4'b0111;  // 7
    parameter zera_timeout   = 4'b1000;  // 8
    parameter comecar_rodada = 4'b1101;  // D
    parameter espera         = 4'b0011;  // 3
    parameter registra       = 4'b0100;  // 4
    parameter comparacao     = 4'b0101;  // 5
    parameter proximo        = 4'b0110;  // 6
    parameter fim_erro       = 4'b1110;  // E
    parameter fim_acerto     = 4'b1010;  // A
    parameter fim_timeout    = 4'b1111;  // F

    // Variaveis de estado
    reg [3:0] Eatual, Eprox;

    reg [14*8-1:0] Eatual_str;
    always@(Eatual) begin
        case(Eatual)
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*/
